# Fritzing sketch BBUNO (saved by Fritzing 1.0.4)
circuit board: 5.64444cm x 6.5cm
breadboards: 1

parts:
  Y1 = Crystal [frequency="16 Mhz" part_number="16 Mhz" package=THT]
  LED1 = LED - 5mm [color="Green (570nm)" current=0.030A package="5 mm [THT]"]
  U2 = Voltage Regulator - 5V [part_number=LM7805 package="TO220 [THT]"]
  R2 = Resistor [tolerance=±5% resistance=220 power=0.25W package=THT]
  R1 = Resistor [tolerance=±5% resistance=10k power=0.25W package=THT]
  C6 = Ceramic Capacitor [capacitance=22pF voltage=35V package="0603 [SMD, multilayer]"]
  C5 = Ceramic Capacitor [capacitance=22pF voltage=35V package="0603 [SMD, multilayer]"]
  C3 = Ceramic Capacitor [capacitance=100nF voltage=35V package="0603 [SMD, multilayer]"]
  12V = Power plug
  U1 = IC, DIP package, 28 pins [chip_label="ATmega 328P"]
  S1 = Momentary Switch [package=ksa_sealed_tac_switch]
  C1 = Electrolytic Capacitor [capacitance=10µF voltage=35V package="100 mil [THT, electrolytic]"]
  C4 = Ceramic Capacitor [capacitance=100nF voltage=35V package="0603 [SMD, multilayer]"]
  ISCP = Adafruit AVR 6-ISP Breakout [part_number="Adafruit #1465"]
  FTDI = FTDI Basic Programmer
  C2 = Electrolytic Capacitor [capacitance=10µF voltage=35V package="100 mil [THT, electrolytic]"]
  C7 = Electrolytic Capacitor [capacitance=1µF voltage=35V package="100 mil [THT, electrolytic]"]

nets (from the breadboard view):
  N1: Y1.pin_0, C6.0, U1.pin10
  N2: Y1.pin_1, C5.1, U1.pin9
  GND: LED1.cathode, U2.GND, C6.1, C5.0, C3.1, 12V.GND, U1.pin8, U1.pin21, C1.-, C4.0, ISCP.GND, FTDI.GND, C2.-
  N3: LED1.anode, R2.Pin_0
  N4: U2.input_voltage, 12V.VCC, C1.+
  N5: U2.output_voltage, R2.Pin_1, R1.Pin_0, C3.0, U1.pin7, U1.pin19, S1.3, C4.1, ISCP.VCC, FTDI.POWER, C2.+
  N6: R1.Pin_1, U1.pin1, S1.2, ISCP.RST, C7.-
  N7: U1.pin3, FTDI.RXI
  N8: U1.pin4, FTDI.TXO
  N9: U1.pin16, ISCP.MOSI
  N10: U1.pin17, ISCP.MISO
  N11: U1.pin18, ISCP.SCK

notes:
  +
  PWR
  Alex Willis
  Arduino Board
  developed with Fritzing
  Pin 13

custom parts:
  Adafruit AVR 6-ISP Breakout: Programming AVR? Always Googling the pinout? Well, now no longer! It's rare to find a mini kit so elegant, it deserves its own Haiku. A simple breakout, 2x3 box header in the center, two 1x3's on the side. Plugs into any breadboard for neat wiring (in both nifty and clean senses of the word). Comes with a quality mini PCB, a 2x3 box header and a small stick of 0.1" header. Requires some light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
